# Fritzing sketch 04_potentiometer_led_and_servo (saved by Fritzing 0.9.1b)
breadboards: 1

parts:
  Part1 = Arduino Uno (Rev3)
  LED1 = LED - 5mm [color="Red (633nm)" package="5 mm [THT]"]
  R2 = Resistor [tolerance=±5% resistance=330 package=THT]
  R3 = Rotary Potentiometer (Small) [maximum_resistance=100kΩ package=THT]
  J1 = Basic Servo

nets:
  N1: Part1.A0, R3.wiper
  N2: Part1.D11_PWM/MOSI, J1.pulse
  N3: Part1.D5_PWM, LED1.anode
  5V: Part1.5V, R3.leg1, J1.vcc
  GND: Part1.GND, R2.Pin_1, R3.leg2, J1.gnd
  N4: LED1.cathode, R2.Pin_0
