# Fritzing sketch 05_keyboard_led_and_servo (saved by Fritzing 0.9.2b)
breadboards: 1

parts:
  Part1 = Arduino Uno (Rev3)
  LED1 = LED - 5mm [color="Red (633nm)" package="5 mm [THT]"]
  R2 = Resistor [tolerance=±5% resistance=330 package=THT]
  J1 = Basic Servo

nets:
  N1: Part1.D11_PWM/MOSI, J1.pulse
  N2: Part1.D5_PWM, LED1.cathode
  5V: Part1.5V, J1.vcc
  GND: Part1.GND, R2.Pin_1, J1.gnd
  N3: LED1.anode, R2.Pin_0
